// Logisim project reptile-hw.circ as structural Verilog: 9 circuits, main circuit main
module main (
);

  wire alu_1_zero, armux, clk, irld, memld, mux, pcinc, pcld, regld, zf, zfld;
  wire [2:0] dst, src1, src2;
  wire [3:0] REGBANK_dout0;
  wire [5:0] aluop;
  wire [11:0] adder_1_out, IR_addr, multiplexer_1_out, multiplexer_4_out, programcounter_1_output, undriven;
  wire [15:0] alu_1_result, multiplexer_2_out, multiplexer_3_out, ram_1_data, REGBANK_dout1, REGBANK_dout2,
       REGBANK_dout3, REGBANK_dout4, REGBANK_dout5, REGBANK_dout6, REGBANK_dout7;
  wire [15:4] REGBANK_dout0_2;
  wire [15:12] multiplexer_4_out_2;

  Adder #(.width(12)) adder_1 (.a(programcounter_1_output), .b(IR_addr), .out(adder_1_out));  // open: cin, cout
  Clock clock_1 (.out(clk));
  Multiplexer #(.width(12), .enable("false")) multiplexer_1 (
    .in0(programcounter_1_output), .in1(undriven), .out(multiplexer_1_out), .sel(armux));
  ProgramCounter programcounter_1 (
    .\input (adder_1_out), .pcld(pcld), .clock(clk), .inc(pcinc), .\output (programcounter_1_output));
  RAM #(.addrWidth(12), .dataWidth(16), .bus("separate")) ram_1 (
    .addr(multiplexer_1_out), .din(multiplexer_3_out), .data(ram_1_data), .str(memld), .clk(clk));  // open: sel, ld, clr
  _1_bit_Register u_1_bit_register_1 (.Din(zfld), .Out(zf), .Load(alu_1_zero), .clk(clk));
  RegisterBank REGBANK (
    .clk(clk), .Dout0({REGBANK_dout0_2, REGBANK_dout0}), .Dout1(REGBANK_dout1), .Dout2(REGBANK_dout2),
    .Dout3(REGBANK_dout3), .Dout4(REGBANK_dout4), .Dout5(REGBANK_dout5), .Dout6(REGBANK_dout6),
    .Dout7(REGBANK_dout7), .regld(regld), .regsel(dst), .Din(multiplexer_2_out));
  Multiplexer #(.width(16), .enable("false")) multiplexer_2 (
    .in0(alu_1_result), .in1(ram_1_data), .out(multiplexer_2_out), .sel(mux));
  Multiplexer #(.select(3), .width(16), .enable("false")) multiplexer_3 (
    .in0({REGBANK_dout0_2, REGBANK_dout0}), .in1(REGBANK_dout1), .in2(REGBANK_dout2), .in3(REGBANK_dout3),
    .in4(REGBANK_dout4), .in5(REGBANK_dout5), .in6(REGBANK_dout6), .in7(REGBANK_dout7),
    .out(multiplexer_3_out), .sel(src1));
  Multiplexer #(.select(3), .width(16), .enable("false")) multiplexer_4 (
    .in0({REGBANK_dout0_2, REGBANK_dout0}), .in1(REGBANK_dout1), .in2(REGBANK_dout2), .in3(REGBANK_dout3),
    .in4(REGBANK_dout4), .in5(REGBANK_dout5), .in6(REGBANK_dout6), .in7(REGBANK_dout7),
    .out({multiplexer_4_out_2, multiplexer_4_out}), .sel(src2));
  ALU alu_1 (
    .a(multiplexer_3_out), .result(alu_1_result), .b({multiplexer_4_out_2, multiplexer_4_out}),
    .Zero(alu_1_zero), .AluOp(aluop));
  InstructionRegister IR (
    .in_1(ram_1_data[11:0]), .load(irld), .addr(IR_addr), .dst(dst), .src2(src1), .src1(src2), .ALUop(aluop),
    .clk(clk));
  Hex_Digit_Display hex_digit_display_1 (.value(REGBANK_dout0_2[15:12]));  // open: dp
  Hex_Digit_Display hex_digit_display_2 (.value(REGBANK_dout0_2[11:8]));  // open: dp
  ControlUnit ControlUnit (
    .ZF(zf), .PCLD(pcld), .PCINC(pcinc), .ARMUX(armux), .REGLD(regld), .ZFLD(zfld), .MUX(mux), .MEMLD(memld),
    .IRLD(irld), .opcode(ram_1_data[15:12]), .clk(clk));
  Hex_Digit_Display hex_digit_display_3 (.value(REGBANK_dout0_2[7:4]));  // open: dp
  Hex_Digit_Display hex_digit_display_4 (.value(REGBANK_dout0));  // open: dp
endmodule

module ALU (
  input  [15:0] a,
  input  [15:0] b,
  input  [5:0] AluOp,
  output [15:0] result,
  output Zero
);

  wire [15:0] adder_1_out, adder_2_out, and_1_out, multiplexer_1_out, not_1_out, or_1_out, subtractor_1_out,
       subtractor_2_out, xor_1_out;

  assign and_1_out = a & b;  // AND_Gate and_1, 16 bits wide
  assign or_1_out = a | b;  // OR_Gate or_1, 16 bits wide
  assign xor_1_out = a ^ b;  // XOR_Gate xor_1, 16 bits wide
  assign not_1_out = ~b;  // NOT_Gate not_1, 16 bits wide
  Adder #(.width(16)) adder_1 (.a(a), .b(b), .out(adder_1_out));  // open: cin, cout
  Subtractor #(.width(16)) subtractor_1 (.a(a), .b(b), .out(subtractor_1_out));  // open: bin, bout
  Adder #(.width(16)) adder_2 (.a(b), .b(16'h1), .out(adder_2_out));  // open: cin, cout
  Subtractor #(.width(16)) subtractor_2 (.a(b), .b(16'h1), .out(subtractor_2_out));  // open: bin, bout
  Multiplexer #(.select(3), .width(16)) multiplexer_1 (
    .in0(not_1_out), .in1(b), .in2(adder_2_out), .in3(subtractor_2_out), .out(multiplexer_1_out),
    .sel(AluOp[2:0]));  // open: in4, in5, in6, in7, en
  Multiplexer #(.select(3), .width(16)) multiplexer_2 (
    .in0(adder_1_out), .in1(subtractor_1_out), .in2(and_1_out), .in3(or_1_out), .in4(xor_1_out),
    .in7(multiplexer_1_out), .out(result), .sel(AluOp[5:3]));  // open: in5, in6, en
  nor zf (Zero, result[0], result[1], result[2], result[3], result[4], result[5], result[6], result[7], result[8], result[9], result[10], result[11], result[12], result[13], result[14], result[15]);
endmodule

module ControlUnit (
  input  [3:0] opcode,
  input  ZF,
  input  clk,
  output PCLD,
  output PCINC,
  output ARMUX,
  output REGLD,
  output ZFLD,
  output MUX,
  output MEMLD,
  output IRLD
);

  wire not_1_out, not_2_out, not_3_out;
  wire [0:0] and_1_out;
  wire [3:0] multiplexer_1_out, multiplexer_2_out, n1_bit_register_1_out;
  wire [8:8] rom_1_data;

  Multiplexer #(.width(4), .enable("false")) multiplexer_1 (
    .in0(4'b0000), .in1(multiplexer_2_out), .out(multiplexer_1_out), .sel(rom_1_data[8]));
  and and_1 (and_1_out[0], not_1_out, not_2_out, opcode[2], not_3_out);
  not not_1 (not_1_out, opcode[0]);
  not not_2 (not_2_out, opcode[1]);
  not not_3 (not_3_out, opcode[3]);
  _1_bit_Register u_1_bit_register_1 (
    .Din(multiplexer_1_out[0]), .Out(n1_bit_register_1_out[0]), .Load(1'b1), .clk(clk));
  _1_bit_Register u_1_bit_register_2 (
    .Din(multiplexer_1_out[1]), .Out(n1_bit_register_1_out[1]), .Load(1'b1), .clk(clk));
  _1_bit_Register u_1_bit_register_3 (
    .Din(multiplexer_1_out[2]), .Out(n1_bit_register_1_out[2]), .Load(1'b1), .clk(clk));
  _1_bit_Register u_1_bit_register_4 (
    .Din(multiplexer_1_out[3]), .Out(n1_bit_register_1_out[3]), .Load(1'b1), .clk(clk));
  Multiplexer #(.select(2), .width(4), .enable("false")) multiplexer_2 (
    .in0(opcode), .in1(opcode), .in2(4'b0000), .in3(4'b0101), .out(multiplexer_2_out),
    .sel({ZF, and_1_out[0]}));
  ROM #(.addrWidth(4), .dataWidth(9)) rom_1 (
    .addr(n1_bit_register_1_out), .data({rom_1_data[8], PCLD, PCINC, ARMUX, REGLD, ZFLD, MUX, MEMLD, IRLD}));  // open: sel

  // Notes on the sheet:
  //   contents of rom_1 (hex, n*v repeats v):
  //   141 54 34 22 0 80 0 18
endmodule

module RegisterBank (
  input  clk,
  input  regld,
  input  [2:0] regsel,
  input  [15:0] Din,
  output [15:0] Dout0,
  output [15:0] Dout1,
  output [15:0] Dout2,
  output [15:0] Dout3,
  output [15:0] Dout4,
  output [15:0] Dout5,
  output [15:0] Dout6,
  output [15:0] Dout7
);

  wire and_1_out, and_2_out, and_3_out, and_4_out, and_5_out, and_6_out, and_7_out, and_8_out,
       decoder_1_out0, decoder_1_out1, decoder_1_out2, decoder_1_out3, decoder_1_out4, decoder_1_out5,
       decoder_1_out6, decoder_1_out7;

  Decoder #(.select(3)) decoder_1 (
    .out0(decoder_1_out0), .out1(decoder_1_out1), .out2(decoder_1_out2), .out3(decoder_1_out3),
    .out4(decoder_1_out4), .out5(decoder_1_out5), .out6(decoder_1_out6), .out7(decoder_1_out7), .sel(regsel));  // open: en
  and and_1 (and_1_out, decoder_1_out0, regld);
  and and_2 (and_2_out, decoder_1_out1, regld);
  and and_3 (and_3_out, decoder_1_out2, regld);
  and and_4 (and_4_out, decoder_1_out3, regld);
  and and_5 (and_5_out, decoder_1_out4, regld);
  and and_6 (and_6_out, decoder_1_out5, regld);
  and and_7 (and_7_out, decoder_1_out6, regld);
  and and_8 (and_8_out, decoder_1_out7, regld);
  _16_bit_Register r0 (.in_1(Din), .out_4(Dout0), .clk(clk), .load(and_1_out));
  _16_bit_Register r1 (.in_1(Din), .out_4(Dout1), .clk(clk), .load(and_2_out));
  _16_bit_Register r2 (.in_1(Din), .out_4(Dout2), .clk(clk), .load(and_3_out));
  _16_bit_Register r3 (.in_1(Din), .out_4(Dout3), .clk(clk), .load(and_4_out));
  _16_bit_Register r4 (.in_1(Din), .out_4(Dout4), .clk(clk), .load(and_5_out));
  _16_bit_Register r5 (.in_1(Din), .out_4(Dout5), .clk(clk), .load(and_6_out));
  _16_bit_Register r6 (.in_1(Din), .out_4(Dout6), .clk(clk), .load(and_7_out));
  _16_bit_Register r7 (.in_1(Din), .out_4(Dout7), .clk(clk), .load(and_8_out));
endmodule

module InstructionRegister (
  input  [11:0] in_1,
  input  load,
  input  clk,
  output [2:0] dst,
  output [2:0] src2,
  output [2:0] src1,
  output [5:0] ALUop,
  output [11:0] addr
);

  _12_bit_Register u_12_bit_register_1 (.load(load), .clk(clk), .out_4(addr), .in_1(in_1));

  assign ALUop = addr[11:6];
  assign dst = addr[2:0];
  assign src1 = addr[8:6];
  assign src2 = addr[5:3];
endmodule

module _1_bit_Register (
  input  Din,
  input  Load,
  input  clk,
  output Out
);

  wire and_1_out, and_2_out, not_1_out;

  not not_1 (not_1_out, Din);
  and and_1 (and_1_out, Din, Load);
  and and_2 (and_2_out, not_1_out, Load);
  S_R_Flip_Flop s_r_ff_1 (.S(and_1_out), .clk(clk), .R(and_2_out), .Q(Out));  // open: Qn, preset, reset, en
endmodule

module _12_bit_Register (
  input  [11:0] in_1,
  input  load,
  input  clk,
  output [11:0] out_4
);

  _1_bit_Register u_1_bit_register_1 (.Din(in_1[0]), .Out(out_4[0]), .Load(load), .clk(clk));
  _1_bit_Register u_1_bit_register_2 (.Din(in_1[1]), .Out(out_4[1]), .Load(load), .clk(clk));
  _1_bit_Register u_1_bit_register_3 (.Din(in_1[2]), .Out(out_4[2]), .Load(load), .clk(clk));
  _1_bit_Register u_1_bit_register_4 (.Din(in_1[3]), .Out(out_4[3]), .Load(load), .clk(clk));
  _1_bit_Register u_1_bit_register_5 (.Din(in_1[4]), .Out(out_4[4]), .Load(load), .clk(clk));
  _1_bit_Register u_1_bit_register_6 (.Din(in_1[5]), .Out(out_4[5]), .Load(load), .clk(clk));
  _1_bit_Register u_1_bit_register_7 (.Din(in_1[6]), .Out(out_4[6]), .Load(load), .clk(clk));
  _1_bit_Register u_1_bit_register_8 (.Din(in_1[7]), .Out(out_4[7]), .Load(load), .clk(clk));
  _1_bit_Register u_1_bit_register_9 (.Din(in_1[8]), .Out(out_4[8]), .Load(load), .clk(clk));
  _1_bit_Register u_1_bit_register_10 (.Din(in_1[9]), .Out(out_4[9]), .Load(load), .clk(clk));
  _1_bit_Register u_1_bit_register_11 (.Din(in_1[10]), .Out(out_4[10]), .Load(load), .clk(clk));
  _1_bit_Register u_1_bit_register_12 (.Din(in_1[11]), .Out(out_4[11]), .Load(load), .clk(clk));
endmodule

// 16-bit
module _16_bit_Register (
  input  [15:0] in_1,
  input  load,
  input  clk,
  output [15:0] out_4
);

  _1_bit_Register u_1_bit_register_1 (.Din(in_1[0]), .Out(out_4[0]), .Load(load), .clk(clk));
  _1_bit_Register u_1_bit_register_2 (.Din(in_1[1]), .Out(out_4[1]), .Load(load), .clk(clk));
  _1_bit_Register u_1_bit_register_3 (.Din(in_1[2]), .Out(out_4[2]), .Load(load), .clk(clk));
  _1_bit_Register u_1_bit_register_4 (.Din(in_1[3]), .Out(out_4[3]), .Load(load), .clk(clk));
  _1_bit_Register u_1_bit_register_5 (.Din(in_1[4]), .Out(out_4[4]), .Load(load), .clk(clk));
  _1_bit_Register u_1_bit_register_6 (.Din(in_1[5]), .Out(out_4[5]), .Load(load), .clk(clk));
  _1_bit_Register u_1_bit_register_7 (.Din(in_1[6]), .Out(out_4[6]), .Load(load), .clk(clk));
  _1_bit_Register u_1_bit_register_8 (.Din(in_1[7]), .Out(out_4[7]), .Load(load), .clk(clk));
  _1_bit_Register u_1_bit_register_9 (.Din(in_1[8]), .Out(out_4[8]), .Load(load), .clk(clk));
  _1_bit_Register u_1_bit_register_10 (.Din(in_1[9]), .Out(out_4[9]), .Load(load), .clk(clk));
  _1_bit_Register u_1_bit_register_11 (.Din(in_1[10]), .Out(out_4[10]), .Load(load), .clk(clk));
  _1_bit_Register u_1_bit_register_12 (.Din(in_1[11]), .Out(out_4[11]), .Load(load), .clk(clk));
  _1_bit_Register u_1_bit_register_13 (.Din(in_1[12]), .Out(out_4[12]), .Load(load), .clk(clk));
  _1_bit_Register u_1_bit_register_14 (.Din(in_1[13]), .Out(out_4[13]), .Load(load), .clk(clk));
  _1_bit_Register u_1_bit_register_15 (.Din(in_1[14]), .Out(out_4[14]), .Load(load), .clk(clk));
  _1_bit_Register u_1_bit_register_16 (.Din(in_1[15]), .Out(out_4[15]), .Load(load), .clk(clk));
endmodule

module ProgramCounter (
  input  [11:0] \input ,
  input  inc,
  input  pcld,
  input  clock,
  output [11:0] \output 
);

  wire or_1_out;
  wire [11:0] adder_1_out, multiplexer_1_out;

  or or_1 (or_1_out, pcld, inc);
  _12_bit_Register u_12_bit_register_1 (.load(or_1_out), .clk(clock), .out_4(\output ), .in_1(multiplexer_1_out));
  Adder #(.width(12)) adder_1 (.a(\output ), .b(12'h1), .out(adder_1_out));  // open: cin, cout
  Multiplexer #(.width(12), .enable("false")) multiplexer_1 (
    .in0(\input ), .in1(adder_1_out), .out(multiplexer_1_out), .sel(inc));
endmodule
